# Fritzing sketch SmartIR (saved by Fritzing 0.9.3b)
breadboards: 1

parts:
  LED1 = smd LED [color="Infrared (880nm)" package="1206 [SMD]"]
  Q1 = NPN-Transistor [package="TO92 [THT]"]
  R1 = Resistor [tolerance=±5% resistance=220 package=THT]
  IR1 = TSOP312.., 314.. [package=THT]
  Raspberry_Pi_2 = Raspberry Pi 3 [part_number=RPI-3-V1.2]
  R2 = Resistor [tolerance=±5% resistance=220 package=THT]

nets:
  N1: LED1.cathode, R1.Pin_1
  N2: LED1.anode, Q1.B
  GND: Q1.E, IR1.GND, Raspberry_Pi_2.GND
  N3: Q1.C, R2.Pin_0
  N4: R1.Pin_0, Raspberry_Pi_2.3v3
  N5: IR1.Vs, Raspberry_Pi_2.GPIO10
  N6: IR1.Data, Raspberry_Pi_2.GPIO24
  N7: Raspberry_Pi_2.GPIO4, R2.Pin_1
